# Fritzing sketch Fritzing_Marco_Vazquez (saved by Fritzing 0.9.2b)
breadboards: 1

parts:
  Parte1 = Arduino Uno (Rev3)
  o1 = Module display OLED I2C 128x64 SSD1306 [package=THT]
  R1 = Rotary Potentiometer (Small) [maximum_resistance=100kΩ package=THT]
  J1 = Piezo Speaker

nets:
  N1: Parte1.A0, R1.wiper
  N2: Parte1.D9_PWM, J1.pin2
  N3: Parte1.A4/SDA, o1.SCL
  N4: Parte1.A5/SCL, o1.SDA
  N5: Parte1.5V, R1.leg2
  GND: Parte1.GND, o1.GND, R1.leg1, J1.pin1

custom parts:
  Module display OLED I2C 128x64 SSD1306: Ecran OLED I2C SSD163 de 128x64 avec connexion I2C
